// Logisim project noughts_and_crosses.circ as structural Verilog
module main (
  input  [23:0] in_1
);

  wire [2:0] led_controller_1_out_2, led_controller_1_out_3, led_controller_1_out_4, led_controller_2_out_2,
       led_controller_2_out_3, led_controller_2_out_4, led_controller_3_out_2, led_controller_3_out_3,
       led_controller_3_out_4, led_controller_4_out_2, led_controller_4_out_3, led_controller_4_out_4,
       led_controller_5_out_2, led_controller_5_out_3, led_controller_5_out_4, led_controller_6_out_2,
       led_controller_6_out_3, led_controller_6_out_4, led_controller_7_out_2, led_controller_7_out_3,
       led_controller_7_out_4, led_controller_8_out_2, led_controller_8_out_3, led_controller_8_out_4,
       led_controller_9_out_2, led_controller_9_out_3, led_controller_9_out_4;

  game_status_controller game_status_controller_1 ();
  led_controller led_controller_1 (
    .in_1(2'b00), .out_2(led_controller_1_out_2), .out_3(led_controller_1_out_3),
    .out_4(led_controller_1_out_4));
  DotMatrix #(.matrixcols(3), .matrixrows(3)) dotmatrix_1 (
    .col0(led_controller_1_out_2), .col1(led_controller_1_out_3), .col2(led_controller_1_out_4));
  led_controller led_controller_2 (
    .out_2(led_controller_2_out_2), .out_3(led_controller_2_out_3), .out_4(led_controller_2_out_4));  // open: in_1
  DotMatrix #(.matrixcols(3), .matrixrows(3)) dotmatrix_2 (
    .col0(led_controller_2_out_2), .col1(led_controller_2_out_3), .col2(led_controller_2_out_4));
  led_controller led_controller_3 (
    .out_2(led_controller_3_out_2), .out_3(led_controller_3_out_3), .out_4(led_controller_3_out_4));  // open: in_1
  DotMatrix #(.matrixcols(3), .matrixrows(3)) dotmatrix_3 (
    .col0(led_controller_3_out_2), .col1(led_controller_3_out_3), .col2(led_controller_3_out_4));
  DotMatrix #(.matrixcols(3), .matrixrows(3)) dotmatrix_4 (
    .col0(led_controller_4_out_2), .col1(led_controller_4_out_3), .col2(led_controller_4_out_4));
  led_controller led_controller_4 (
    .in_1(2'b11), .out_2(led_controller_4_out_2), .out_3(led_controller_4_out_3),
    .out_4(led_controller_4_out_4));
  led_controller led_controller_5 (
    .out_2(led_controller_5_out_2), .out_3(led_controller_5_out_3), .out_4(led_controller_5_out_4));  // open: in_1
  DotMatrix #(.matrixcols(3), .matrixrows(3)) dotmatrix_5 (
    .col0(led_controller_5_out_2), .col1(led_controller_5_out_3), .col2(led_controller_5_out_4));
  DotMatrix #(.matrixcols(3), .matrixrows(3)) dotmatrix_6 (
    .col0(led_controller_6_out_2), .col1(led_controller_6_out_3), .col2(led_controller_6_out_4));
  led_controller led_controller_6 (
    .out_2(led_controller_6_out_2), .out_3(led_controller_6_out_3), .out_4(led_controller_6_out_4));  // open: in_1
  led_controller led_controller_7 (
    .in_1(2'b10), .out_2(led_controller_7_out_2), .out_3(led_controller_7_out_3),
    .out_4(led_controller_7_out_4));
  DotMatrix #(.matrixcols(3), .matrixrows(3)) dotmatrix_7 (
    .col0(led_controller_7_out_2), .col1(led_controller_7_out_3), .col2(led_controller_7_out_4));
  led_controller led_controller_8 (
    .out_2(led_controller_8_out_2), .out_3(led_controller_8_out_3), .out_4(led_controller_8_out_4));  // open: in_1
  DotMatrix #(.matrixcols(3), .matrixrows(3)) dotmatrix_8 (
    .col0(led_controller_8_out_2), .col1(led_controller_8_out_3), .col2(led_controller_8_out_4));
  DotMatrix #(.matrixcols(3), .matrixrows(3)) dotmatrix_9 (
    .col0(led_controller_9_out_2), .col1(led_controller_9_out_3), .col2(led_controller_9_out_4));
  led_controller led_controller_9 (
    .out_2(led_controller_9_out_2), .out_3(led_controller_9_out_3), .out_4(led_controller_9_out_4));  // open: in_1
endmodule

module led_controller (
  input  [1:0] in_1,
  output [2:0] out_2,
  output [2:0] out_3,
  output [2:0] out_4
);

  wire not_1_out;
  wire [8:0] multiplexer_1_out;

  Multiplexer #(.width(9), .enable("false")) multiplexer_1 (
    .in0(9'h1ef), .in1(9'h155), .out(multiplexer_1_out), .sel(in_1[0]));
  not not_1 (not_1_out, in_1[1]);
  Multiplexer #(.width(9), .enable("false")) multiplexer_2 (
    .in0(multiplexer_1_out), .in1({9{1'b0}}), .out({out_4, out_3, out_2}), .sel(not_1_out));
endmodule
